// Logisim project bcd_subtractor_2digit.circ as structural Verilog
module bcd_subtractor_2digit (
  input  A0,
  input  B0,
  input  A1,
  input  B1,
  input  A2,
  input  B2,
  input  A3,
  input  B3,
  input  A4,
  input  B4,
  input  A5,
  input  B5,
  input  A6,
  input  B6,
  input  A7,
  input  B7,
  input  Bin,
  input  GND,
  output D0,
  output D1,
  output D2,
  output D3,
  output D4,
  output D5,
  output D6,
  output D7,
  output Borrow
);

  wire A11_out, A12_out, A13_out, A14_out, A31_out, A32_out, A33_out, A34_out, A41_out, A42_out, A43_out,
       A44_out, and_1_out, and_2_out, and_3_out, and_4_out, and_5_out, and_6_out, and_7_out, and_8_out,
       and_9_out, and_10_out, and_11_out, and_12_out, and_13_out, and_14_out, and_15_out, and_16_out,
       and_17_out, and_18_out, and_19_out, and_20_out, and_21_out, and_22_out, and_23_out, and_24_out,
       B2J9_out, B2J22_out, B2K9_out, B2K22_out, B2L9_out, B2L22_out, B2T9_out, B2T22_out, B11_out, B12_out,
       B13_out, B14_out, B31_out, B32_out, B33_out, B34_out, B41_out, B42_out, B43_out, B44_out, C11_out,
       C12_out, C13_out, C14_out, C31_out, C32_out, C33_out, C34_out, C41_out, C42_out, C43_out, C44_out,
       G11_out, G12_out, G13_out, G14_out, G31_out, G32_out, G33_out, G34_out, G41_out, G42_out, G43_out,
       N1_out, N2_out, NB_out, NBIN_out, not_1_out, not_2_out, not_3_out, O1_out, or_1_out, or_2_out,
       or_3_out, or_4_out, or_5_out, or_6_out, or_7_out, or_8_out, or_9_out, or_10_out, or_12_out, or_13_out,
       or_14_out, or_15_out, or_16_out, or_17_out, or_18_out, or_19_out, or_20_out, or_21_out, or_22_out,
       or_23_out, or_24_out, or_25_out, S11_out, S12_out, S13_out, S14_out, S31_out, S32_out, S33_out,
       S34_out, X2_out, X3_out, X11_out, X12_out, X13_out, X14_out, X31_out, X32_out, X33_out, X34_out,
       X41_out, X42_out, X43_out, X44_out, xor_1_out, xor_2_out, xor_3_out, xor_4_out, xor_5_out, xor_6_out,
       xor_7_out, xor_8_out, xor_9_out, xor_11_out, xor_12_out, xor_13_out, xor_15_out, xor_16_out,
       xor_17_out, xor_18_out, xor_19_out, xor_20_out, xor_21_out, xor_22_out, xor_23_out, xor_24_out;

  not not_1 (not_1_out, B0);
  xor X2 (X2_out, B2, B1);
  or or_1 (or_1_out, B2, B1);
  xor X3 (X3_out, B3, or_1_out);
  not not_2 (not_2_out, X3_out);
  xor xor_1 (xor_1_out, A0, not_1_out);
  xor xor_2 (xor_2_out, xor_1_out, GND);
  and A11 (A11_out, A0, not_1_out);
  and and_1 (and_1_out, GND, xor_1_out);
  or C11 (C11_out, A11_out, and_1_out);
  or G11 (G11_out, C11_out, GND);
  xor xor_3 (xor_3_out, A1, B1);
  xor xor_4 (xor_4_out, xor_3_out, G11_out);
  and and_2 (and_2_out, A1, B1);
  and B12 (B12_out, G11_out, xor_3_out);
  or C12 (C12_out, and_2_out, B12_out);
  or or_2 (or_2_out, C12_out, GND);
  xor X13 (X13_out, A2, X2_out);
  xor S13 (S13_out, X13_out, or_2_out);
  and A13 (A13_out, A2, X2_out);
  and and_3 (and_3_out, or_2_out, X13_out);
  or C13 (C13_out, A13_out, and_3_out);
  or or_3 (or_3_out, C13_out, GND);
  xor X14 (X14_out, A3, not_2_out);
  xor xor_5 (xor_5_out, X14_out, or_3_out);
  and and_4 (and_4_out, A3, not_2_out);
  and B14 (B14_out, or_3_out, X14_out);
  or or_4 (or_4_out, and_4_out, B14_out);
  or G14 (G14_out, or_4_out, GND);
  not NBIN (NBIN_out, Bin);
  xor X31 (X31_out, xor_2_out, NBIN_out);
  xor xor_6 (xor_6_out, X31_out, GND);
  and and_5 (and_5_out, xor_2_out, NBIN_out);
  and and_6 (and_6_out, GND, X31_out);
  or or_5 (or_5_out, and_5_out, and_6_out);
  or G31 (G31_out, or_5_out, GND);
  xor xor_7 (xor_7_out, xor_4_out, GND);
  xor S32 (S32_out, xor_7_out, G31_out);
  and A32 (A32_out, xor_4_out, GND);
  and B32 (B32_out, G31_out, xor_7_out);
  or C32 (C32_out, A32_out, B32_out);
  or G32 (G32_out, C32_out, GND);
  xor xor_8 (xor_8_out, S13_out, GND);
  xor S33 (S33_out, xor_8_out, G32_out);
  and A33 (A33_out, S13_out, GND);
  and and_7 (and_7_out, G32_out, xor_8_out);
  or or_6 (or_6_out, A33_out, and_7_out);
  or or_7 (or_7_out, or_6_out, GND);
  xor X34 (X34_out, xor_5_out, GND);
  xor S34 (S34_out, X34_out, or_7_out);
  and and_8 (and_8_out, xor_5_out, GND);
  and B34 (B34_out, or_7_out, X34_out);
  or C34 (C34_out, and_8_out, B34_out);
  or or_8 (or_8_out, C34_out, GND);
  or B2J9 (B2J9_out, B2T9_out, B2K9_out);
  and B2K9 (B2K9_out, B2L9_out, S34_out);
  or B2L9 (B2L9_out, S33_out, S32_out);
  or B2T9 (B2T9_out, G14_out, or_8_out);
  xor xor_9 (xor_9_out, xor_6_out, GND);
  xor xor_10 (D0, xor_9_out, GND);
  and A41 (A41_out, xor_6_out, GND);
  and B41 (B41_out, GND, xor_9_out);
  or C41 (C41_out, A41_out, B41_out);
  or or_9 (or_9_out, C41_out, GND);
  xor xor_11 (xor_11_out, S32_out, B2J9_out);
  xor S42 (D1, xor_11_out, or_9_out);
  and and_9 (and_9_out, S32_out, B2J9_out);
  and B42 (B42_out, or_9_out, xor_11_out);
  or or_10 (or_10_out, and_9_out, B42_out);
  or G42 (G42_out, or_10_out, GND);
  xor xor_12 (xor_12_out, S33_out, B2J9_out);
  xor S43 (D2, xor_12_out, G42_out);
  and and_10 (and_10_out, S33_out, B2J9_out);
  and and_11 (and_11_out, G42_out, xor_12_out);
  or C43 (C43_out, and_10_out, and_11_out);
  or G43 (G43_out, C43_out, GND);
  xor xor_13 (xor_13_out, S34_out, GND);
  xor xor_14 (D3, xor_13_out, G43_out);
  and and_12 (and_12_out, S34_out, GND);
  and B44 (B44_out, G43_out, xor_13_out);
  or C44 (C44_out, and_12_out, B44_out);
  // OR_Gate or_11 has open pins: in0=C44_out, in1=GND, out=open
  not NB (NB_out, B2J9_out);
  not N1 (N1_out, B4);
  xor xor_15 (xor_15_out, B6, B5);
  or O1 (O1_out, B6, B5);
  xor xor_16 (xor_16_out, B7, O1_out);
  not N2 (N2_out, xor_16_out);
  xor X11 (X11_out, A4, N1_out);
  xor S11 (S11_out, X11_out, GND);
  and and_13 (and_13_out, A4, N1_out);
  and B11 (B11_out, GND, X11_out);
  or or_12 (or_12_out, and_13_out, B11_out);
  or or_13 (or_13_out, or_12_out, GND);
  xor X12 (X12_out, A5, B5);
  xor S12 (S12_out, X12_out, or_13_out);
  and A12 (A12_out, A5, B5);
  and and_14 (and_14_out, or_13_out, X12_out);
  or or_14 (or_14_out, A12_out, and_14_out);
  or G12 (G12_out, or_14_out, GND);
  xor xor_17 (xor_17_out, A6, xor_15_out);
  xor xor_18 (xor_18_out, xor_17_out, G12_out);
  and and_15 (and_15_out, A6, xor_15_out);
  and B13 (B13_out, G12_out, xor_17_out);
  or or_15 (or_15_out, and_15_out, B13_out);
  or G13 (G13_out, or_15_out, GND);
  xor xor_19 (xor_19_out, A7, N2_out);
  xor S14 (S14_out, xor_19_out, G13_out);
  and A14 (A14_out, A7, N2_out);
  and and_16 (and_16_out, G13_out, xor_19_out);
  or C14 (C14_out, A14_out, and_16_out);
  or or_16 (or_16_out, C14_out, GND);
  not not_3 (not_3_out, NB_out);
  xor xor_20 (xor_20_out, S11_out, not_3_out);
  xor S31 (S31_out, xor_20_out, GND);
  and A31 (A31_out, S11_out, not_3_out);
  and B31 (B31_out, GND, xor_20_out);
  or C31 (C31_out, A31_out, B31_out);
  or or_17 (or_17_out, C31_out, GND);
  xor X32 (X32_out, S12_out, GND);
  xor xor_21 (xor_21_out, X32_out, or_17_out);
  and and_17 (and_17_out, S12_out, GND);
  and and_18 (and_18_out, or_17_out, X32_out);
  or or_18 (or_18_out, and_17_out, and_18_out);
  or or_19 (or_19_out, or_18_out, GND);
  xor X33 (X33_out, xor_18_out, GND);
  xor xor_22 (xor_22_out, X33_out, or_19_out);
  and and_19 (and_19_out, xor_18_out, GND);
  and B33 (B33_out, or_19_out, X33_out);
  or C33 (C33_out, and_19_out, B33_out);
  or G33 (G33_out, C33_out, GND);
  xor xor_23 (xor_23_out, S14_out, GND);
  xor xor_24 (xor_24_out, xor_23_out, G33_out);
  and A34 (A34_out, S14_out, GND);
  and and_20 (and_20_out, G33_out, xor_23_out);
  or or_20 (or_20_out, A34_out, and_20_out);
  or G34 (G34_out, or_20_out, GND);
  or B2J22 (B2J22_out, B2T22_out, B2K22_out);
  and B2K22 (B2K22_out, B2L22_out, xor_24_out);
  or B2L22 (B2L22_out, xor_22_out, xor_21_out);
  or B2T22 (B2T22_out, or_16_out, G34_out);
  xor X41 (X41_out, S31_out, GND);
  xor S41 (D4, X41_out, GND);
  and and_21 (and_21_out, S31_out, GND);
  and and_22 (and_22_out, GND, X41_out);
  or or_21 (or_21_out, and_21_out, and_22_out);
  or G41 (G41_out, or_21_out, GND);
  xor X42 (X42_out, xor_21_out, B2J22_out);
  xor xor_25 (D5, X42_out, G41_out);
  and A42 (A42_out, xor_21_out, B2J22_out);
  and and_23 (and_23_out, G41_out, X42_out);
  or C42 (C42_out, A42_out, and_23_out);
  or or_22 (or_22_out, C42_out, GND);
  xor X43 (X43_out, xor_22_out, B2J22_out);
  xor xor_26 (D6, X43_out, or_22_out);
  and A43 (A43_out, xor_22_out, B2J22_out);
  and B43 (B43_out, or_22_out, X43_out);
  or or_23 (or_23_out, A43_out, B43_out);
  or or_24 (or_24_out, or_23_out, GND);
  xor X44 (X44_out, xor_24_out, GND);
  xor S44 (D7, X44_out, or_24_out);
  and A44 (A44_out, xor_24_out, GND);
  and and_24 (and_24_out, or_24_out, X44_out);
  or or_25 (or_25_out, A44_out, and_24_out);
  // OR_Gate G44 has open pins: in0=or_25_out, in1=GND, out=open
  not not_4 (Borrow, B2J22_out);
endmodule
