// Logisim project mux_8to1.circ as structural Verilog
module mux_8to1 (
  input  D0,
  input  S0,
  input  D1,
  input  S1,
  input  D2,
  input  S2,
  input  D3,
  input  D4,
  input  D5,
  input  D6,
  input  D7,
  output Y
);

  wire n1, n2, n3, n4, n5, n8, n10, n13, n15, n18, n20, n23, n25, n28, n30, n33, n35, n38, n40, n45, n47,
       n49, n51, n53, n55, n57, n59, n60, n61, n62, n63, n64, n65;

  and MUX0S1 (n3, n1, n2);
  and MUX0S2 (n5, n3, n4);
  and MUX1S1 (n8, S0, n2);
  and MUX1S2 (n10, n8, n4);
  and MUX2S1 (n13, n1, S1);
  and MUX2S2 (n15, n13, n4);
  and MUX3S1 (n18, S0, S1);
  and MUX3S2 (n20, n18, n4);
  and MUX4S1 (n23, n1, n2);
  and MUX4S2 (n25, n23, S2);
  and MUX5S1 (n28, S0, n2);
  and MUX5S2 (n30, n28, S2);
  and MUX6S1 (n33, n1, S1);
  and MUX6S2 (n35, n33, S2);
  and MUX7S1 (n38, S0, S1);
  and MUX7S2 (n40, n38, S2);
  not MUXN1 (n1, S0);
  not MUXN2 (n2, S1);
  not MUXN3 (n4, S2);
  and MUX0D (n45, D0, n5);
  and MUX1D (n47, D1, n10);
  and MUX2D (n49, D2, n15);
  and MUX3D (n51, D3, n20);
  and MUX4D (n53, D4, n25);
  and MUX5D (n55, D5, n30);
  and MUX6D (n57, D6, n35);
  and MUX7D (n59, D7, n40);
  or MUXO1 (n60, n45, n47);
  or MUXO2 (n61, n60, n49);
  or MUXO3 (n62, n61, n51);
  or MUXO4 (n63, n62, n53);
  or MUXO5 (n64, n63, n55);
  or MUXO6 (n65, n64, n57);
  or MUXO7 (Y, n65, n59);

  // Other names for the same wires on the sheet: n6 = S0; n16 = S0; n26 = S0; n36 = S0; n41 = S0; n7 = n2; n22 = n2;
  //   n27 = n2; n9 = n4; n14 = n4; n19 = n4; n11 = n1; n21 = n1; n31 = n1; n12 = S1; n17 = S1; n32 = S1; n37 = S1;
  //   n42 = S1; n24 = S2; n29 = S2; n34 = S2; n39 = S2; n43 = S2; n44 = D0; n46 = D1; n48 = D2; n50 = D3; n52 = D4;
  //   n54 = D5; n56 = D6; n58 = D7; n66 = Y
endmodule
