// Logisim project subtractor_4bit.circ as structural Verilog
module subtractor_4bit (
  input  A0,
  input  B0,
  input  A1,
  input  B1,
  input  A2,
  input  B2,
  input  A3,
  input  B3,
  input  Bin,
  output D0,
  output D1,
  output D2,
  output D3,
  output Bout
);

  wire n9, n13, n14, n16, n17, n18, n19, n22, n23, n25, n26, n27, n28, n31, n32, n34, n35, n36, n37, n40,
       n41, n43, n44;

  xor SUB0X (n9, A0, B0);
  xor SUB0D (D0, n9, Bin);
  not SUB0N (n13, A0);
  or SUB0O (n14, B0, Bin);
  and SUB0A (n16, n13, n14);
  and SUB0B (n17, B0, Bin);
  or SUB0C (n19, n16, n17);
  xor SUB1X (n18, A1, B1);
  xor SUB1D (D1, n18, n19);
  not SUB1N (n22, A1);
  or SUB1O (n23, B1, n19);
  and SUB1A (n25, n22, n23);
  and SUB1B (n26, B1, n19);
  or SUB1C (n28, n25, n26);
  xor SUB2X (n27, A2, B2);
  xor SUB2D (D2, n27, n28);
  not SUB2N (n31, A2);
  or SUB2O (n32, B2, n28);
  and SUB2A (n34, n31, n32);
  and SUB2B (n35, B2, n28);
  or SUB2C (n37, n34, n35);
  xor SUB3X (n36, A3, B3);
  xor SUB3D (D3, n36, n37);
  not SUB3N (n40, A3);
  or SUB3O (n41, B3, n37);
  and SUB3A (n43, n40, n41);
  and SUB3B (n44, B3, n37);
  or SUB3C (Bout, n43, n44);

  // Other names for the same wires on the sheet: n1 = A0; n2 = B0; n3 = A1; n4 = B1; n5 = A2; n6 = B2; n7 = A3;
  //   n8 = B3; n11 = D0; n10 = Bin; n12 = Bin; n15 = Bin; n20 = D1; n21 = n19; n24 = n19; n29 = D2; n30 = n28;
  //   n33 = n28; n38 = D3; n39 = n37; n42 = n37; n45 = Bout
endmodule
